# Fritzing sketch OTA_VCA_wIVC_Test (saved by Fritzing 0.9.3b)
breadboards: 1

parts:
  IC1 = Dual Op-Amp [package=dip08]
  C1 = Ceramic Capacitor [capacitance=100nF package="100 mil [THT, multilayer]"]
  R1 = TRIMPOT [package=3362u-2]
  C3 = Ceramic Capacitor [capacitance=100nF package="100 mil [THT, multilayer]"]
  R3 = Resistor [tolerance=±5% resistance=4.7k package=THT]
  IC2 = IC, DIP package, 16 pins [chip_label=NJM13600]
  R4 = Resistor [tolerance=±5% resistance=33k package=THT]
  R5 = Resistor [tolerance=±5% resistance=4.7k package=THT]
  C4 = Electrolytic Capacitor [capacitance=1µF package="100 mil [THT, electrolytic]"]
  C5 = Ceramic Capacitor [capacitance=100nF package="100 mil [THT, multilayer]"]
  C6 = Ceramic Capacitor [capacitance=100nF package="100 mil [THT, multilayer]"]
  C7 = Electrolytic Capacitor [capacitance=1µF package="100 mil [THT, electrolytic]"]
  C8 = Electrolytic Capacitor [capacitance=1µF package="100 mil [THT, electrolytic]"]
  LED1 = LED - 3mm [color="Green (570nm)" package="3 mm [THT]"]
  R7 = Resistor [tolerance=±5% resistance=10k package=THT]
  R8 = Resistor [tolerance=±5% resistance=22k package=THT]
  VCC1 = Battery
  VCC2 = Battery
  R6 = Resistor [tolerance=±5% resistance=100k package=THT]
  Q1 = PNP-Transistor [package="TO92 [THT]"]
  R9 = Resistor [tolerance=±5% resistance=10k package=THT]
  R10 = Resistor [tolerance=±5% resistance=1k package=THT]
  R11 = TRIMPOT [package=3362u-2]
  C9 = Electrolytic Capacitor [capacitance=1µF package="100 mil [THT, electrolytic]"]
  C10 = Electrolytic Capacitor [capacitance=1µF package="100 mil [THT, electrolytic]"]

nets:
  N1: IC1.A_OUT, Q1.C
  N2: IC1.A_-IN, R9.Pin_1, R10.Pin_0
  N3: IC1.A_+IN, IC1.B_+IN, C1.0, C3.0, IC2.pin4, IC2.pin14, R4.Pin_1, R5.Pin_1, C5.0, C6.0, C7.-, C8.+, VCC1.-, R6.Pin_1, R11.CCW, C10.-
  N4: IC1.A_V-, C3.1, R3.Pin_1, IC2.pin6, C5.1, C8.-, R7.Pin_1, VCC2.+
  N5: IC1.B_-IN, IC1.B_OUT
  N6: IC1.A_V+, C1.1, IC2.pin11, C6.1, C7.+, LED1.anode, VCC1.+
  N7: R1.WIPER, R1.CW, R9.Pin_0, C10.+
  N8: R3.Pin_0, IC2.pin8, C4.-
  N9: IC2.pin1, Q1.B
  N10: IC2.pin3, R5.Pin_0, C9.-
  N11: IC2.pin5, IC2.pin7, R4.Pin_0
  N12: IC2.pin10, IC2.pin12, IC2.pin13
  N13: C4.+, R6.Pin_0
  N14: LED1.cathode, R7.Pin_0
  N15: R8.Pin_1, R11.CW
  N16: Q1.E, R10.Pin_1
  N17: R11.WIPER, C9.+

notes:
  V-
  GND
  GND
  V+
  BIAS In
  NJM13700
  1 AMP BIAS INPUT A 16 AMP BIAS INPUT B
  2 DIODE BIAS A 15 DIODE BIAS B
  3 +INPUT A 14 +INPUT B
  4 -INPUT A 13 -INPUT B
  5 OUTPUT A 12 OUTPUT B
  6 V- 11 V+
  7 BUFFER INPUT A 10 BUFFER INPUT B
  8 BUFFER OUTPUT A 9 BUFFER OUTPUT B
  Wave In
  Wave Out
  5V
